# Fritzing sketch uln2003_wiring_diagram (saved by Fritzing 0.9.3b)

parts:
  X113647 = X113647 Stepper Driver Board [part_number=X113647 package=board]
  UNO = Arduino Uno (Rev3)
  MOTOR1 = 28BYJ-48 Stepper Motor
  5V = Power plug

nets:
  N1: X113647.IN1, UNO.D8
  N2: X113647.IN2, UNO.D9_PWM
  N3: X113647.IN3, UNO.D10_PWM/SS
  N4: X113647.IN4, UNO.D11_PWM/MOSI
  GND: X113647.GND, UNO.GND, 5V.GND
  VIN: X113647.+V, UNO.VIN, 5V.VCC
  N5: X113647.BLUE, MOTOR1.BLUE
  N6: X113647.PINK, MOTOR1.PINK
  N7: X113647.YELLOW, MOTOR1.YELLOW
  N8: X113647.ORANGE, MOTOR1.ORANGE
  N9: X113647.RED, MOTOR1.RED

custom parts:
  X113647 Stepper Driver Board: A common stepper motor driver board based on ULN2003APG darlington array
  28BYJ-48 Stepper Motor: 28BYJ-48 gear-reduction stepper motor (small)
